// Logisim project mct4.circ as structural Verilog: 2 circuits, main circuit main
module main (
  input  in_1
);

  wire and_1_out, and_2_out, apu_1_carry, clock_1_out, comparator_1_eq, or_1_out, Reset_out, Step_out,
       t_ff_1_q, ToggleClock_out;
  wire [1:0] Carry_q;
  wire [2:0] counter_1_q;
  wire [3:0] binary_to_bcd_converter_1_p2, binary_to_bcd_converter_1_p3, binary_to_bcd_converter_1_p4,
       controlled_buffer_1_out, MAR_q, PC_q;
  wire [7:0] A_q, apu_1_sum, B_q, IR_q, ram_1_dout, register_1_q, undriven;
  wire [7:4] controlled_buffer_1_out_2;
  wire [15:0] rom_1_data;

  RAM #(.addrWidth(4), .enables("line")) ram_1 (
    .addr(MAR_q), .we(rom_1_data[6]), .clk(or_1_out),
    .din({controlled_buffer_1_out_2, controlled_buffer_1_out}), .dout(ram_1_dout));
  Counter #(.max('h7), .width(3)) counter_1 (
    .clr(Reset_out), .load(rom_1_data[15]), .up(1'b1), .count(1'b1), .clk(or_1_out), .D(3'b000),
    .Q(counter_1_q));  // open: carry
  Register #(.width(4)) MAR (
    .D(controlled_buffer_1_out), .en(rom_1_data[8]), .clk(or_1_out), .Q(MAR_q), .clr(Reset_out));
  Register IR (
    .D({controlled_buffer_1_out_2, controlled_buffer_1_out}), .en(rom_1_data[4]), .clk(or_1_out), .Q(IR_q),
    .clr(Reset_out));
  LED led_1 (.in(t_ff_1_q));
  Button ToggleClock (.out(ToggleClock_out));
  Button Step (.out(Step_out));
  Button Reset (.out(Reset_out));
  assign {controlled_buffer_1_out_2, controlled_buffer_1_out} = rom_1_data[7] ? ram_1_dout : 8'bz;  // Controlled_Buffer controlled_buffer_1
  ROM #(.addrWidth(9), .dataWidth(16)) rom_1 (.addr({IR_q[7:4], Carry_q, counter_1_q}), .data(rom_1_data));
  T_Flip_Flop t_ff_1 (.T(1'b1), .clk(ToggleClock_out), .Q(t_ff_1_q), .reset(rom_1_data[0]));  // open: Qn, preset
  assign {controlled_buffer_1_out_2, controlled_buffer_1_out} = rom_1_data[5] ? {4'b0000, IR_q[3:0]} : 8'bz;  // Controlled_Buffer controlled_buffer_2
  Clock clock_1 (.out(clock_1_out));
  and and_1 (and_1_out, clock_1_out, t_ff_1_q);
  or or_1 (or_1_out, Step_out, and_1_out);
  LedBar ledbar_1 (
    .led0(controlled_buffer_1_out_2[7]), .led1(controlled_buffer_1_out_2[6]),
    .led2(controlled_buffer_1_out_2[5]), .led3(controlled_buffer_1_out_2[4]),
    .led4(controlled_buffer_1_out[3]), .led5(controlled_buffer_1_out[2]), .led6(controlled_buffer_1_out[1]),
    .led7(controlled_buffer_1_out[0]));
  // DipSwitch dipswitch_1: pin names not known
  assign {controlled_buffer_1_out_2, controlled_buffer_1_out} = in_1 ? undriven : 8'bz;  // Controlled_Buffer controlled_buffer_3
  Register A (
    .D({controlled_buffer_1_out_2, controlled_buffer_1_out}), .en(rom_1_data[9]), .clk(or_1_out), .Q(A_q),
    .clr(Reset_out));
  Register B (
    .D({controlled_buffer_1_out_2, controlled_buffer_1_out}), .en(rom_1_data[11]), .clk(or_1_out), .Q(B_q),
    .clr(Reset_out));
  assign {controlled_buffer_1_out_2, controlled_buffer_1_out} = rom_1_data[10] ? A_q : 8'bz;  // Controlled_Buffer controlled_buffer_4
  assign {controlled_buffer_1_out_2, controlled_buffer_1_out} = rom_1_data[12] ? apu_1_sum : 8'bz;  // Controlled_Buffer controlled_buffer_5
  assign {controlled_buffer_1_out_2, controlled_buffer_1_out} = rom_1_data[2] ? {4'b0000, PC_q} : 8'bz;  // Controlled_Buffer controlled_buffer_6
  Counter #(.max('hf), .width(4)) PC (
    .clr(Reset_out), .load(rom_1_data[1]), .up(1'b1), .count(rom_1_data[3]), .clk(or_1_out),
    .D(controlled_buffer_1_out), .Q(PC_q));  // open: carry
  Register register_1 (
    .D({controlled_buffer_1_out_2, controlled_buffer_1_out}), .en(rom_1_data[14]), .clk(or_1_out),
    .Q(register_1_q), .clr(Reset_out));
  apu apu_1 (.A(A_q), .B(B_q), .AS(rom_1_data[13]), .sum(apu_1_sum), .carry(apu_1_carry));
  Hex_Digit_Display hex_digit_display_1 (.value(register_1_q[7:4]));  // open: dp
  Hex_Digit_Display hex_digit_display_2 (.value(binary_to_bcd_converter_1_p2));  // open: dp
  // Binary_to_BCD_converter #(.binvalue(8)) binary_to_bcd_converter_1: pin names not known; wires that end beside it: register_1_q, binary_to_bcd_converter_1_p2, binary_to_bcd_converter_1_p3, binary_to_bcd_converter_1_p4
  D_Flip_Flop Carry (.D(apu_1_carry), .clk(and_2_out), .Q(Carry_q[0]), .reset(Reset_out));  // open: Qn, preset
  D_Flip_Flop Zero (.D(comparator_1_eq), .clk(and_2_out), .Q(Carry_q[1]), .reset(Reset_out));  // open: Qn, preset
  Comparator comparator_1 (.a(apu_1_sum), .b({8{1'b0}}), .eq(comparator_1_eq));  // open: gt, lt
  and and_2 (and_2_out, or_1_out, rom_1_data[12]);
  Hex_Digit_Display hex_digit_display_3 (.value(register_1_q[3:0]));  // open: dp
  Hex_Digit_Display hex_digit_display_4 (.value(binary_to_bcd_converter_1_p3));  // open: dp
  Hex_Digit_Display hex_digit_display_5 (.value(binary_to_bcd_converter_1_p4));  // open: dp

  // Notes on the sheet:
  //   contents of rom_1 (hex, n*v repeats v):
  //   104 98 8000 5*0 104 98 8000 5*0 104 98 8000 5*0 104 98 8000 5*0 104 98 8220 5*0 104 98 8220 5*0 104
  //   98 8220 5*0 104 98 8220 5*0 104 98 120 8280 4*0 104 98 120 8280 4*0 104 98 120 8280 4*0 104 98 120
  //   8280 4*0 104 98 120 8440 4*0 104 98 120 8440 4*0 104 98 120 8440 4*0 104 98 120 8440 4*0 104 98 8000
  //   5*0 104 98 8000 5*0 104 98 8000 5*0 104 98 8000 5*0 104 98 120 880 9200 0 0 0 104 98 120 880 9200 0
  //   0 0 104 98 120 880 9200 0 0 0 104 98 120 880 9200 0 0 0 104 98 120 880 b200 0 0 0 104 98 120 880
  //   b200 0 0 0 104 98 120 880 b200 0 0 0 104 98 120 880 b200 0 0 0 104 98 c400 5*0 104 98 c400 5*0 104
  //   98 c400 5*0 104 98 c400 5*0 104 98 8022 5*0 104 98 8022 5*0 104 98 8022 5*0 104 98 8022 5*0 104 98
  //   8000 5*0 104 98 8000 5*0 104 98 8022 5*0 104 98 8022 5*0 104 98 8000 5*0 104 98 8022 5*0 104 98 8000
  //   5*0 104 98 8022 5*0 104 98 8000 5*0 104 98 8000 5*0 104 98 8000 5*0 104 98 8000 5*0 104 98 8000 5*0
  //   104 98 8000 5*0 104 98 8000 5*0 104 98 8000 5*0 104 98 8000 5*0 104 98 8000 5*0 104 98 8000 5*0 104
  //   98 8000 5*0 104 98 8000 5*0 104 98 8000 5*0 104 98 8000 5*0 104 98 8000 5*0 104 98 1 5*0 104 98 1
  //   5*0 104 98 1 5*0 104 98 1
endmodule

module apu (
  input  [7:0] A,
  input  [7:0] B,
  input  AS,
  output [7:0] sum,
  output carry
);

  wire adder_1_cout, subtractor_1_bout;
  wire [7:0] adder_1_out, subtractor_1_out;

  Adder adder_1 (.a(A), .b(B), .out(adder_1_out), .cout(adder_1_cout));  // open: cin
  Subtractor subtractor_1 (.a(A), .b(B), .out(subtractor_1_out), .bout(subtractor_1_bout));  // open: bin
  Multiplexer #(.width(8)) multiplexer_1 (.in0(adder_1_out), .in1(subtractor_1_out), .out(sum), .sel(AS));
  Multiplexer multiplexer_2 (.in0(adder_1_cout), .in1(subtractor_1_bout), .out(carry), .sel(AS));
endmodule
